# Fritzing sketch file 26 (saved by Fritzing 0.9.4)
breadboards: 1

parts:
  SP1 = SPEAKER [package=pcb_mount_speaker]
  Part1 = Arduino Uno (Rev3)
  S1 = Pushbutton [package="[THT]"]

nets:
  N1: SP1.+, Part1.GND
  N2: SP1.-, Part1.D8
  N3: Part1.D7, S1.Pin_3, S1.Pin_4
