# Fritzing sketch file 28 (saved by Fritzing 0.9.4)
breadboards: 1

parts:
  DHT1 = Humidity and Temperature Sensor DHT11
  Part1 = Arduino Uno (Rev3)
  R1 = Resistor [tolerance=±5% resistance=220 package=THT]

nets:
  VCC: DHT1.Vcc, Part1.5V
  N1: DHT1.Data-signal, Part1.D2, R1.Pin_0
  N2: DHT1.GND_2, Part1.GND

custom parts:
  Humidity and Temperature Sensor DHT11: Digital relative humidity & temperature sensor DHT11
