# Fritzing sketch file 29 (saved by Fritzing 0.9.4)
breadboards: 1

parts:
  DHT1 = Humidity and Temperature Sensor DHT11
  Part1 = Arduino Uno (Rev3)
  R1 = Resistor [tolerance=±5% resistance=220 package=THT]
  LCD1 = LCD screen
  U1 = POT [package=pot_mammoth]

nets:
  VCC: DHT1.Vcc, Part1.D7, Part1.5V, LCD1.VDD, LCD1.R/W, LCD1.LED+, U1.S
  N1: DHT1.Data-signal, R1.Pin_0
  GND: DHT1.GND_2, Part1.GND, LCD1.VSS, LCD1.LED-, U1.E
  N2: Part1.D11_PWM/MOSI, LCD1.E
  N3: Part1.D12/MISO, LCD1.RS
  N4: Part1.D2, LCD1.DB7
  N5: Part1.D3_PWM, LCD1.DB6
  N6: Part1.D4, LCD1.DB5
  N7: Part1.D5_PWM, LCD1.DB4
  N8: LCD1.V0, U1.A

custom parts:
  Humidity and Temperature Sensor DHT11: Digital relative humidity & temperature sensor DHT11
