# Fritzing sketch file 30 (saved by Fritzing 0.9.4)
breadboards: 1

parts:
  SP1 = SPEAKER [package=pcb_mount_speaker]
  Part1 = Arduino Uno (Rev3)
  S1 = Pushbutton [package="[THT]"]
  S2 = Pushbutton [package="[THT]"]
  S3 = Pushbutton [package="[THT]"]
  S4 = Pushbutton [package="[THT]"]

nets:
  N1: SP1.+, Part1.GND, S1.Pin_1, S1.Pin_2, S2.Pin_1, S2.Pin_2, S3.Pin_1, S3.Pin_2, S4.Pin_1, S4.Pin_2
  N2: SP1.-, Part1.D12/MISO
  N3: Part1.D8, S4.Pin_3, S4.Pin_4
  N4: Part1.D5_PWM, S1.Pin_3, S1.Pin_4
  N5: Part1.D6_PWM, S2.Pin_3, S2.Pin_4
  N6: Part1.D7, S3.Pin_3, S3.Pin_4
